// Logisim project SOMADOR8BITS.circ as structural Verilog: 6 circuits, main circuit main
module main (
  input  [7:0] VALOR_A,
  input  OP,
  input  [7:0] VALOR_B,
  output out_4,
  output out_5,
  output [7:0] RESULTADO
);

  wire op_1_out_3, op_1_out_4, op_1_out_5, op_1_out_6, op_1_out_7, op_1_out_8, op_1_out_9, op_1_out_10,
       somador_bit_a_bit_1_cout7, somador_bit_a_bit_1_cout8;

  OP op_1 (
    .OP(OP), .VALOR2(VALOR_B), .out_3(op_1_out_3), .out_4(op_1_out_4), .out_5(op_1_out_5),
    .out_6(op_1_out_6), .out_7(op_1_out_7), .out_8(op_1_out_8), .out_9(op_1_out_9), .out_10(op_1_out_10));
  SOMADOR_BIT_A_BIT somador_bit_a_bit_1 (
    .A0(VALOR_A[0]), .B0(op_1_out_3), .C0(OP), .A1(VALOR_A[1]), .B1(op_1_out_4), .A2(VALOR_A[2]),
    .B2(op_1_out_5), .A3(VALOR_A[3]), .B3(op_1_out_6), .A4(VALOR_A[4]), .B4(op_1_out_7), .A5(VALOR_A[5]),
    .B5(op_1_out_8), .A6(VALOR_A[6]), .B6(op_1_out_9), .A7(VALOR_A[7]), .B7(op_1_out_10), .S0(RESULTADO[0]),
    .S1(RESULTADO[1]), .S2(RESULTADO[2]), .S3(RESULTADO[3]), .S4(RESULTADO[4]), .S5(RESULTADO[5]),
    .S6(RESULTADO[6]), .S7(RESULTADO[7]), .Cout7(somador_bit_a_bit_1_cout7), .Cout8(somador_bit_a_bit_1_cout8));
  OVERFLOW overflow_1 (
    .OP(OP), .C7(somador_bit_a_bit_1_cout7), .C8(somador_bit_a_bit_1_cout8), .OVERFLOW_SEM_SINAL(out_4),
    .OVERFLOW_COM_SINAL(out_5));

  // Notes on the sheet:
  //   0 ADI
  //   1 SUB
  //   SOMADOR
  //   OVERFLOW SEM SINAL
  //   OVERFLOW COM SINAL
endmodule

module SOMADOR_BIT_A_BIT (
  input  A0,
  input  B0,
  input  C0,
  input  A1,
  input  B1,
  input  A2,
  input  B2,
  input  A3,
  input  B3,
  input  A4,
  input  B4,
  input  A5,
  input  B5,
  input  A6,
  input  B6,
  input  A7,
  input  B7,
  output S0,
  output S1,
  output S2,
  output S3,
  output S4,
  output S5,
  output S6,
  output S7,
  output Cout7,
  output Cout8
);

  wire Cout_2_out_4, Cout_3_out_4, Cout_4_out_4, Cout_5_out_4, Cout_6_out_4, Cout_out_4;

  COUT_1_BIT Cout (.A(A0), .B(B0), .Cin(C0), .out_4(Cout_out_4));
  SOMA_1_BIT SOMA (.BIT_A(A0), .BIT_B(B0), .CARRY_IN(C0), .out_4(S0));
  COUT_1_BIT Cout_2 (.A(A1), .B(B1), .Cin(Cout_out_4), .out_4(Cout_2_out_4));
  SOMA_1_BIT SOMA_2 (.BIT_A(A1), .BIT_B(B1), .CARRY_IN(Cout_out_4), .out_4(S1));
  COUT_1_BIT Cout_3 (.A(A2), .B(B2), .Cin(Cout_2_out_4), .out_4(Cout_3_out_4));
  SOMA_1_BIT SOMA_3 (.BIT_A(A2), .BIT_B(B2), .CARRY_IN(Cout_2_out_4), .out_4(S2));
  COUT_1_BIT Cout_4 (.A(A3), .B(B3), .Cin(Cout_3_out_4), .out_4(Cout_4_out_4));
  SOMA_1_BIT SOMA_4 (.BIT_A(A3), .BIT_B(B3), .CARRY_IN(Cout_3_out_4), .out_4(S3));
  COUT_1_BIT Cout_5 (.A(A4), .B(B4), .Cin(Cout_4_out_4), .out_4(Cout_5_out_4));
  SOMA_1_BIT SOMA_5 (.BIT_A(A4), .BIT_B(B4), .CARRY_IN(Cout_4_out_4), .out_4(S4));
  COUT_1_BIT Cout_6 (.A(A5), .B(B5), .Cin(Cout_5_out_4), .out_4(Cout_6_out_4));
  SOMA_1_BIT SOMA_6 (.BIT_A(A5), .BIT_B(B5), .CARRY_IN(Cout_5_out_4), .out_4(S5));
  COUT_1_BIT Cout_7 (.A(A6), .B(B6), .Cin(Cout_6_out_4), .out_4(Cout7));
  SOMA_1_BIT SOMA_7 (.BIT_A(A6), .BIT_B(B6), .CARRY_IN(Cout_6_out_4), .out_4(S6));
  COUT_1_BIT Cout_8 (.A(A7), .B(B7), .Cin(Cout7), .out_4(Cout8));
  SOMA_1_BIT SOMA_8 (.BIT_A(A7), .BIT_B(B7), .CARRY_IN(Cout7), .out_4(S7));
endmodule

module SOMA_1_BIT (
  input  BIT_A,
  input  BIT_B,
  input  CARRY_IN,
  output out_4
);

  wire A_B_C_out, A_nB_nC_out, nA_B_nC_out, nA_nB_C_out, not_1_out, not_2_out, not_3_out;

  not not_1 (not_1_out, BIT_A);
  not not_2 (not_2_out, BIT_B);
  not not_3 (not_3_out, CARRY_IN);
  and nA_nB_C (nA_nB_C_out, not_1_out, not_2_out, CARRY_IN);
  and nA_B_nC (nA_B_nC_out, not_1_out, BIT_B, not_3_out);
  and A_nB_nC (A_nB_nC_out, BIT_A, not_2_out, not_3_out);
  and A_B_C (A_B_C_out, BIT_A, BIT_B, CARRY_IN);
  or or_1 (out_4, nA_nB_C_out, nA_B_nC_out, A_nB_nC_out, A_B_C_out);
endmodule

module COUT_1_BIT (
  input  A,
  input  B,
  input  Cin,
  output out_4
);

  wire A_B_C_out, A_B_nC_out, A_nB_C_out, nA_B_C_out, not_1_out, not_2_out, not_3_out;

  not not_1 (not_1_out, A);
  not not_2 (not_2_out, B);
  not not_3 (not_3_out, Cin);
  and nA_B_C (nA_B_C_out, not_1_out, B, Cin);
  and A_nB_C (A_nB_C_out, A, not_2_out, Cin);
  and A_B_nC (A_B_nC_out, not_3_out, B, A);
  and A_B_C (A_B_C_out, A, B, Cin);
  or or_1 (out_4, nA_B_C_out, A_nB_C_out, A_B_nC_out, A_B_C_out);
endmodule

module OP (
  input  OP,
  input  [7:0] VALOR2,
  output out_3,
  output out_4,
  output out_5,
  output out_6,
  output out_7,
  output out_8,
  output out_9,
  output out_10
);

  xor xor_1 (out_3, VALOR2[0], OP);
  xor xor_2 (out_4, VALOR2[1], OP);
  xor xor_3 (out_5, VALOR2[2], OP);
  xor xor_4 (out_6, VALOR2[3], OP);
  xor xor_5 (out_7, VALOR2[4], OP);
  xor xor_6 (out_8, VALOR2[5], OP);
  xor xor_7 (out_9, VALOR2[6], OP);
  xor xor_8 (out_10, VALOR2[7], OP);
endmodule

module OVERFLOW (
  input  OP,
  input  C7,
  input  C8,
  output OVERFLOW_SEM_SINAL,
  output OVERFLOW_COM_SINAL
);

  wire xor_1_out, xor_2_out, xor_3_out, xor_4_out;

  xor xor_1 (xor_1_out, OP, C8);
  xor xor_2 (xor_2_out, OP, C8);
  xor xor_3 (xor_3_out, C7, C8);
  xor xor_4 (xor_4_out, C8, C7);
  or or_1 (OVERFLOW_SEM_SINAL, xor_1_out, xor_2_out);
  or or_2 (OVERFLOW_COM_SINAL, xor_3_out, xor_4_out);
endmodule
